# Fritzing sketch Arduino-RPi Sketch (saved by Fritzing 0.9.3b)
breadboards: 1

parts:
  U2 = L298 [package=multiwatt15_6400bgheatsink]
  Raspberry_Pi1 = Raspberry Pi 2
  Part2 = Arduino Uno (Rev3) - ICSP
  M1 = DC Motor
  M2 = DC Motor

nets:
  N1: U2.OUT1, M2.pin_2
  N2: U2.OUT2, M2.pin_1
  N3: U2.VS, Part2.5V
  N4: U2.IN1, Part2.ICSP_MISO, Part2.D12/MISO
  N5: U2.ENA, Part2.D11_PWM/MOSI
  N6: U2.IN2, Part2.D13/SCK
  GND: U2.GND, Raspberry_Pi1.GND, Part2.GND
  N7: U2.IN3, Part2.D2
  N8: U2.ENB, Part2.D3_PWM
  N9: U2.IN4, Part2.D4
  N10: U2.OUT3, M1.pin_2
  N11: U2.OUT4, M1.pin_1
  N12: Raspberry_Pi1.GPIO2, Part2.A4/SDA
  N13: Raspberry_Pi1.GPIO3, Part2.A5/SCL

notes:
  From the X8R to the Arduino
  Pin 5 goes to RSSI
  Pin 6 goes to Channel 5
  Pin 9 goes to Channel 1
  Pin 10 goes to Channel 3
