# Fritzing sketch RGB Sensor (saved by Fritzing 0.9.2b)
breadboards: 1

parts:
  SENSOR1 = TCS34725 RGB Color Sensor
  Part1 = Arduino Uno (Rev3)
  LED1 = RGB LED - (4 legs) [package="5 mm [THT]"]
  R1 = Resistor [tolerance=±5% resistance=220 package="0603 [SMD]"]

nets:
  N1: SENSOR1.LED, Part1.D5_PWM
  N2: SENSOR1.SDA, Part1.A4/SDA
  N3: SENSOR1.SCL, Part1.A5/SCL
  GND: SENSOR1.GND, Part1.GND, LED1.green_cathode
  VDD: SENSOR1.VDD, Part1.5V, LED1.common_anode
  N4: Part1.D6_PWM, R1.Pin_1
  N5: LED1.red_cathode, R1.Pin_0

custom parts:
  TCS34725 RGB Color Sensor: TCS34725 RGB Color Sensor with LED

// code stored in the sketch: neopixlecolornew.ino
#include <Wire.h>
#include "Adafruit_TCS34725.h"
#include <Adafruit_NeoPixel.h>
 
// Parameter 1 = number of pixels in strip
// Parameter 2 = pin number (most are valid)
// Parameter 3 = pixel type flags, add together as needed:
//   NEO_RGB     Pixels are wired for RGB bitstream
//   NEO_GRB     Pixels are wired for GRB bitstream
//   NEO_KHZ400  400 KHz bitstream (e.g. FLORA pixels)
//   NEO_KHZ800  800 KHz bitstream (e.g. High Density LED strip)
Adafruit_NeoPixel strip = Adafruit_NeoPixel(1, 6, NEO_RGB + NEO_KHZ800);
//led pin for led on RGB sensor
int led = 5;

// our RGB -> eye-recognized gamma color
byte gammatable[256];
 
Adafruit_TCS34725 tcs = Adafruit_TCS34725(TCS34725_INTEGRATIONTIME_50MS, TCS34725_GAIN_4X);
 
void setup() {
  Serial.begin(9600);
  Serial.println("Color View Test!");

  pinMode(led, OUTPUT);
  
  strip.begin();
  strip.show(); // Initialize all pixels to 'off'
  
  if (tcs.begin()) {
    Serial.println("Found sensor");
  } else {
    Serial.println("No TCS34725 found ... check your connections");
    while (1); // halt!
  }
  
  // thanks PhilB for this gamma table!
  // it helps convert RGB colors to what humans see
  for (int i=0; i<256; i++) {
    float x = i;
    x /= 255;
    x = pow(x, 2.5);
    x *= 255;
      
    gammatable[i] = x;      
    //Serial.println(gammatable[i]);
  }
  
//  for (int i=0; i<3; i++){ //this sequence flashes the first pixel three times as a countdown to the color reading.
//    strip.setPixelColor (0, strip.Color(188, 188, 188)); //white, but dimmer-- 255 for all three values makes it blinding!
//    strip.show();
//    delay(1000);
//    strip.setPixelColor (0, strip.Color(0, 0, 0));
//    strip.show();
//    delay(500);
//  }
}
 
// Fill the dots one after the other with a color
void colorWipe(uint32_t c, uint8_t wait) {
  for(uint16_t i=0; i<strip.numPixels(); i++) {
      strip.setPixelColor(i, c);
      strip.show();
      delay(wait);
  }
}

void loop() {
  digitalWrite(led,LOW);
  //loop is empty because it only takes the color reading once on power up! Turn the scarf off and on again to change the color.
  uint16_t clear, red, green, blue; 
  tcs.setInterrupt(false);      // turn on LED
  delay(60);  // takes 50ms to read 
  tcs.getRawData(&red, &green, &blue, &clear); 
  tcs.setInterrupt(true);  // turn off LED  
  Serial.print("C:\t"); Serial.print(clear);
  Serial.print("\tR:\t"); Serial.print(red);
  Serial.print("\tG:\t"); Serial.print(green);
  Serial.print("\tB:\t"); Serial.print(blue);
  // Figure out some basic hex code for visualization
  uint32_t sum = red;
  sum += green;
  sum += blue;
  sum += clear;
  float r, g, b;
  r = red; r /= sum;
  g = green; g /= sum;
  b = blue; b /= sum;
  r *= 256; g *= 256; b *= 256;
  Serial.print("\t");
  Serial.print((int)r, HEX); Serial.print((int)g, HEX); Serial.print((int)b, HEX);
  Serial.println();
 
  Serial.print((int)r ); Serial.print(" "); Serial.print((int)g);Serial.print(" ");  Serial.println((int)b );
  colorWipe(strip.Color(gammatable[(int)r], gammatable[(int)g], gammatable[(int)b]), 50);
}
